// Logisim project cerrojo_logica.circ as structural Verilog: 4 circuits, main circuit main
module main (
  input  P0,
  input  P1,
  input  P2,
  input  P3,
  input  P4,
  input  P5,
  input  P6,
  input  P7,
  input  P8
);

  wire decodificador_abrir_1_abrir, decodificador_cerrar_1_cerrar, latch_sr_1_abrirlatch,
       latch_sr_1_cerrarlatch;

  Decodificador_Abrir decodificador_abrir_1 (
    .P0(P0), .P1(P1), .P2(P2), .P3(P3), .P4(P4), .P5(P5), .P6(P6), .P7(P7), .P8(P8),
    .Abrir(decodificador_abrir_1_abrir));
  Decodificador_Cerrar decodificador_cerrar_1 (
    .P0(P0), .P1(P1), .P2(P2), .P3(P3), .P4(P4), .P5(P5), .P6(P6), .P7(P7), .P8(P8),
    .Cerrar(decodificador_cerrar_1_cerrar));
  LED led_1 (.in(latch_sr_1_abrirlatch));
  Latch_SR latch_sr_1 (
    .Abrir(decodificador_abrir_1_abrir), .Cerrar(decodificador_cerrar_1_cerrar),
    .AbrirLatch(latch_sr_1_abrirlatch), .CerrarLatch(latch_sr_1_cerrarlatch));
  LED led_2 (.in(latch_sr_1_cerrarlatch));
endmodule

module Decodificador_Abrir (
  input  P0,
  input  P1,
  input  P2,
  input  P3,
  input  P4,
  input  P5,
  input  P6,
  input  P7,
  input  P8,
  output Abrir
);

  wire not_1_out, not_2_out, not_3_out, not_4_out, not_5_out;

  not not_1 (not_1_out, P0);
  not not_2 (not_2_out, P1);
  not not_3 (not_3_out, P4);
  not not_4 (not_4_out, P5);
  not not_5 (not_5_out, P8);
  and and_1 (Abrir, not_1_out, not_2_out, P2, P3, not_3_out, not_4_out, P6, P7, not_5_out);
endmodule

module Decodificador_Cerrar (
  input  P0,
  input  P1,
  input  P2,
  input  P3,
  input  P4,
  input  P5,
  input  P6,
  input  P7,
  input  P8,
  output Cerrar
);

  wire not_1_out, not_2_out, not_3_out, not_4_out, not_5_out, not_6_out;

  not not_1 (not_1_out, P1);
  not not_2 (not_2_out, P2);
  not not_3 (not_3_out, P3);
  not not_4 (not_4_out, P4);
  not not_5 (not_5_out, P6);
  not not_6 (not_6_out, P8);
  and and_1 (Cerrar, P0, not_1_out, not_2_out, not_3_out, not_4_out, P5, not_5_out, P7, not_6_out);
endmodule

module Latch_SR (
  input  Abrir,
  input  Cerrar,
  output AbrirLatch,
  output CerrarLatch
);

  nor nor_1 (CerrarLatch, Abrir, AbrirLatch);
  nor nor_2 (AbrirLatch, CerrarLatch, Cerrar);
endmodule
